# Fritzing sketch Sintuino (saved by Fritzing 0.9.3b)
breadboards: 1

parts:
  hc-sr1 = hc-sr04
  hc-sr2 = hc-sr04
  R1 = Trimmer Potentiometer [maximum_resistance=10kΩ package=THT]
  R3 = Trimmer Potentiometer [maximum_resistance=10kΩ package=THT]
  SP1 = SPEAKER [package=pcb_mount_speaker]
  R5 = Trimmer Potentiometer [maximum_resistance=10kΩ package=THT]
  Part1 = Arduino Uno (Rev3)
  LED1 = smd LED [color="Red (633nm)" package="0603 [SMD]"]
  S1 = Pushbutton [package="[THT]"]

nets:
  VCC: hc-sr1.VCC, hc-sr2.VCC, R1.leg2, R3.leg2, R5.leg2, Part1.5V
  N1: hc-sr1.Trig, Part1.D7
  N2: hc-sr1.Echo, Part1.D8
  GND: hc-sr1.GND, hc-sr2.GND, R1.leg1, R3.leg1, SP1.+, R5.leg1, Part1.GND, LED1.anode, S1.Pin_1, S1.Pin_2
  N3: hc-sr2.Trig, Part1.D11_PWM/MOSI
  N4: hc-sr2.Echo, Part1.D12/MISO
  N5: R1.wiper, Part1.A0
  N6: R3.wiper, Part1.A2
  N7: SP1.-, Part1.D9_PWM
  N8: R5.wiper, Part1.A1
  N9: Part1.D2, S1.Pin_3, S1.Pin_4
  N10: Part1.D4, LED1.cathode
