# Fritzing sketch progetto_synth_tremolo (saved by Fritzing 0.9.3b)
breadboards: 1

parts:
  Part1 = Arduino Uno (Rev3)
  hc-sr1 = hc-sr04
  hc-sr2 = hc-sr04
  R1 = Trimmer Potentiometer [maximum_resistance=10kΩ package=THT]
  R2 = Trimmer Potentiometer [maximum_resistance=10kΩ package=THT]
  R3 = Trimmer Potentiometer [maximum_resistance=10kΩ package=THT]
  SP1 = SPEAKER [package=pcb_mount_speaker]
  R4 = Trimmer Potentiometer [maximum_resistance=10kΩ package=THT]
  R5 = Trimmer Potentiometer [maximum_resistance=10kΩ package=THT]

nets:
  N1: Part1.A0, R1.wiper
  N2: Part1.A1, R5.wiper
  N3: Part1.A2, R3.wiper
  N4: Part1.A3, R4.wiper
  N5: Part1.A4/SDA, R2.wiper
  N6: Part1.D9_PWM, SP1.-
  N7: Part1.D10_PWM/SS, hc-sr1.Trig
  N8: Part1.D11_PWM/MOSI, hc-sr1.Echo
  N9: Part1.D12/MISO, hc-sr2.Trig
  N10: Part1.D13/SCK, hc-sr2.Echo
  GND: Part1.GND, hc-sr1.GND, hc-sr2.GND, R1.leg1, R2.leg1, R3.leg1, SP1.+, R4.leg1, R5.leg1
  VCC: Part1.5V, hc-sr1.VCC, hc-sr2.VCC, R1.leg2, R2.leg2, R3.leg2, R4.leg2, R5.leg2
